// Logisim project Basic4Bit.circ as structural Verilog: 1 circuit, main circuit main
module main (
  input  in_1,
  input  [7:0] in_2
);

  wire A_pin7, A_pin10, AB, ADD, adder_1_cout, ALUOP, and_1_out, and_2_out, and_3_out, and_4_out, and_5_out,
       and_7_out, and_8_out, and_9_out, and_10_out, and_11_out, and_12_out, B_pin7, B_pin10, C_q, CLK, CMP,
       Decode, Execute, Fetch, INST_pin7, INST_pin10, instNAND, JPC, JPZ, LDI, LDST, n74138_1_pin4,
       n74138_1_pin5, n74138_1_pin6, nAB, nCLK, nDecode, nExecute, nFetch, nor_1_out, not_3_out, not_5_out,
       not_6_out, not_10_out, not_11_out, not_12_out, not_13_out, not_14_out, not_15_out, not_16_out,
       not_17_out, nRESET, nStore, or_2_out, outputA, outputB, outputTEMP, PCH_pin2, PCH_pin7, PCH_pin9,
       PCH_pin10, PCL_pin7, PCL_pin9, PCL_pin10, PT, pull_resistor_2_node, Store, TEMP_pin7, TEMP_pin10, wrA,
       wrB;
  wire [1:1] Start_p1;
  wire [2:0] INST;
  wire [3:0] adder_1_out, AOUT, BOUT, controlled_buffer_7_out, DATA, nand_1_out, PCH_pin14, PCL_pin14,
       TEMPOUT;
  wire [7:0] ADDRESS, DATAEXT, PCH_pin3;

  Clock clock_1 (.out(CLK));
  // DipSwitch Start: pin names not known; wires that end beside it: Start_p1[1]
  not not_1 (nRESET, in_1);
  T_Flip_Flop t_ff_1 (.T(1'b1), .clk(CLK), .Q(Start_p1[1]));  // open: Qn, reset, preset
  _74161 #(.ShowInternalStructure("true")) PCH (
    .pin1(nRESET), .pin2(PCH_pin2), .pin3(PCH_pin3[0]), .pin4(PCH_pin3[1]), .pin5(PCH_pin3[2]),
    .pin6(PCH_pin3[3]), .pin7(PCH_pin7), .pin14(PCH_pin14[0]), .pin13(PCH_pin14[1]), .pin12(PCH_pin14[2]),
    .pin11(PCH_pin14[3]), .pin10(PCH_pin10), .pin9(PCH_pin9));  // open: pin15
  _74161 #(.ShowInternalStructure("true")) PCL (
    .pin1(nRESET), .pin2(Store), .pin3(PCH_pin3[4]), .pin4(PCH_pin3[5]), .pin5(PCH_pin3[6]),
    .pin6(PCH_pin3[7]), .pin7(PCL_pin7), .pin15(PCH_pin2), .pin14(PCL_pin14[0]), .pin13(PCL_pin14[1]),
    .pin12(PCL_pin14[2]), .pin11(PCL_pin14[3]), .pin10(PCL_pin10), .pin9(PCL_pin9));
  Demultiplexer #(.select(2)) demultiplexer_1 (
    .out0(Fetch), .out1(Store), .out2(Execute), .out3(Decode), .in(1'b1), .sel({Start_p1[1], CLK}));
  not not_2 (nCLK, CLK);
  RAM #(.asyncread("true"), .databus("bidir"), .\type ("nonvolatile")) FRAM (
    .addr(ADDRESS), .we(not_3_out), .oe(LDST), .clk(nStore), .data(DATAEXT));
  not not_3 (not_3_out, LDST);
  not not_4 (nDecode, Decode);
  assign ADDRESS = not_5_out ? {PCH_pin14, PCL_pin14} : 8'bz;  // Controlled_Buffer controlled_buffer_1
  not not_5 (not_5_out, and_1_out);
  assign ADDRESS = and_1_out ? {4'b1111, BOUT} : 8'bz;  // Controlled_Buffer controlled_buffer_2
  and and_1 (and_1_out, Store, not_6_out);
  not not_6 (not_6_out, LDST);
  not not_7 (nFetch, Fetch);
  not not_8 (nStore, Store);
  not not_9 (nExecute, Execute);
  Pull_Resistor pull_resistor_1 (.node(ADDRESS));
  Hex_Digit_Display #(.decimalPoint("false")) hex_digit_display_1 (.value(AOUT));
  Hex_Digit_Display #(.decimalPoint("false")) hex_digit_display_2 (.value(DATA));
  Hex_Digit_Display #(.decimalPoint("false")) hex_digit_display_3 (.value({3'b101, AB}));
  Hex_Digit_Display #(.decimalPoint("false")) hex_digit_display_4 (.value(BOUT));
  Hex_Digit_Display #(.decimalPoint("false")) hex_digit_display_5 (.value(ADDRESS[7:4]));
  Hex_Digit_Display #(.decimalPoint("false")) hex_digit_display_6 (.value({1'b0, INST}));
  Hex_Digit_Display #(.decimalPoint("false")) hex_digit_display_7 (.value(ADDRESS[3:0]));
  Hex_Digit_Display #(.decimalPoint("false")) hex_digit_display_8 (.value(TEMPOUT));
  _74161 #(.ShowInternalStructure("true")) A (
    .pin1(nRESET), .pin2(Store), .pin3(DATA[0]), .pin4(DATA[1]), .pin5(DATA[2]), .pin6(DATA[3]),
    .pin7(A_pin7), .pin14(AOUT[0]), .pin13(AOUT[1]), .pin12(AOUT[2]), .pin11(AOUT[3]), .pin10(A_pin10),
    .pin9(wrA));  // open: pin15
  _74161 #(.ShowInternalStructure("true")) B (
    .pin1(nRESET), .pin2(Store), .pin3(DATA[0]), .pin4(DATA[1]), .pin5(DATA[2]), .pin6(DATA[3]),
    .pin7(B_pin7), .pin14(BOUT[0]), .pin13(BOUT[1]), .pin12(BOUT[2]), .pin11(BOUT[3]), .pin10(B_pin10),
    .pin9(wrB));  // open: pin15
  D_Flip_Flop C (.D(adder_1_cout), .clk(ADD), .Q(C_q));  // open: Qn, preset, reset
  _74161 #(.ShowInternalStructure("true")) u_INST (
    .pin1(nRESET), .pin2(CLK), .pin3(DATAEXT[0]), .pin4(DATAEXT[1]), .pin5(DATAEXT[2]), .pin6(DATAEXT[3]),
    .pin7(INST_pin7), .pin14(INST[0]), .pin13(INST[1]), .pin12(INST[2]), .pin11(AB), .pin10(INST_pin10),
    .pin9(nFetch));  // open: pin15
  assign DATA = nor_1_out ? DATAEXT[7:4] : 4'bz;  // Controlled_Buffer controlled_buffer_3
  nor nor_1 (nor_1_out, outputTEMP, outputB, outputA);
  assign DATA = outputA ? AOUT : 4'bz;  // Controlled_Buffer controlled_buffer_4
  assign DATA = outputB ? BOUT : 4'bz;  // Controlled_Buffer controlled_buffer_5
  assign DATA = outputTEMP ? TEMPOUT : 4'bz;  // Controlled_Buffer controlled_buffer_6
  Adder #(.width(4)) adder_1 (.a(DATA), .b(AOUT), .out(adder_1_out), .cin(C_q), .cout(adder_1_cout));
  assign controlled_buffer_7_out = instNAND ? adder_1_out : 4'bz;  // Controlled_Buffer controlled_buffer_7
  not not_10 (not_10_out, instNAND);
  assign nand_1_out = ~(AOUT & DATA);  // NAND_Gate nand_1, 4 bits wide
  assign controlled_buffer_7_out = not_10_out ? nand_1_out : 4'bz;  // Controlled_Buffer controlled_buffer_8
  and and_2 (and_2_out, LDI, PT);
  not not_11 (not_11_out, INST[1]);
  not not_12 (not_12_out, INST[0]);
  _74161 #(.ShowInternalStructure("true")) TEMP (
    .pin1(nRESET), .pin2(Execute), .pin3(controlled_buffer_7_out[0]), .pin4(controlled_buffer_7_out[1]),
    .pin5(controlled_buffer_7_out[2]), .pin6(controlled_buffer_7_out[3]), .pin7(TEMP_pin7),
    .pin14(TEMPOUT[0]), .pin13(TEMPOUT[1]), .pin12(TEMPOUT[2]), .pin11(TEMPOUT[3]), .pin10(TEMP_pin10),
    .pin9(ALUOP));  // open: pin15
  or or_1 (wrB, and_2_out, nAB);
  and and_3 (and_3_out, INST[2], INST[0]);
  and and_4 (and_4_out, INST[2], INST[1]);
  and and_5 (and_5_out, not_12_out, not_11_out, AB);
  _74138 #(.ShowInternalStructure("true")) u_74138_1 (
    .pin1(INST[0]), .pin2(INST[1]), .pin3(INST[2]), .pin4(n74138_1_pin4), .pin5(n74138_1_pin5),
    .pin6(n74138_1_pin6), .pin7(JPC), .pin15(LDI), .pin14(PT), .pin13(ADD), .pin12(instNAND), .pin11(LDST),
    .pin10(CMP), .pin9(JPZ));
  _7414 #(.ShowInternalStructure("true")) u_7414_1 (
    .pin13(AB), .pin12(nAB));  // open: pin1, pin2, pin3, pin4, pin5, pin6, pin11, pin10, pin9, pin8
  or or_2 (or_2_out, and_3_out, and_4_out, and_5_out);
  or or_3 (wrA, or_2_out, nStore);
  _7400 #(.ShowInternalStructure("true")) u_7400_1 ();  // open: pin1, pin2, pin3, pin4, pin5, pin6, pin13, pin12, pin11, pin10, pin9, pin8
  and and_6 (ALUOP, ADD, instNAND);
  not not_13 (not_13_out, ALUOP);
  and and_7 (and_7_out, AB, not_13_out);
  not not_14 (not_14_out, PT);
  not not_15 (not_15_out, LDST);
  not not_16 (not_16_out, PT);
  not not_17 (not_17_out, PT);
  and and_8 (and_8_out, not_17_out, nAB, CLK);
  and and_9 (and_9_out, nCLK, and_7_out);
  and and_10 (and_10_out, not_13_out, CLK);
  and and_11 (and_11_out, CLK, not_14_out, not_15_out, nAB);
  and and_12 (and_12_out, not_16_out, AB, CLK);
  or or_4 (outputA, and_12_out, pull_resistor_2_node);
  Pull_Resistor pull_resistor_2 (.node(pull_resistor_2_node));
  or or_5 (outputB, and_8_out, and_9_out);
  or or_6 (outputTEMP, and_10_out, and_11_out);
  // also tied to GND on the sheet: {A_pin7, A_pin10, INST_pin7, B_pin7, INST_pin10, B_pin10, TEMP_pin7, TEMP_pin10, n74138_1_pin4, n74138_1_pin5}
  // also tied to VCC on the sheet: {PCH_pin7, PCL_pin7, PCH_pin10, PCH_pin9, PCL_pin10, PCL_pin9, n74138_1_pin6}

  // Other names for the same wires on the sheet: DATAEXTMANUAL[7:0] = in_2; RESET = in_1

  // Notes on the sheet:
  //   Registers
endmodule
